// Logisim project esercizio2.circ as structural Verilog: 1 circuit, main circuit main
module main (
  input  A,
  input  B,
  input  C,
  output out_4
);

  wire and_1_out, nand_1_out, nand_2_out, nand_3_out, xor_1_out;

  xor xor_1 (xor_1_out, A, B);
  nand nand_1 (nand_1_out, C, C);
  nand nand_2 (nand_2_out, xor_1_out, xor_1_out);
  nand nand_3 (nand_3_out, xor_1_out, C);
  and and_1 (and_1_out, nand_1_out, nand_2_out);
  nand nand_4 (out_4, nand_3_out, and_1_out);
endmodule
