// Logisim project esercizio_2_esame_2014.circ as structural Verilog: 1 circuit, main circuit main
module main (
  input  in_1,
  input  in_2,
  input  in_3,
  input  in_4,
  input  C,
  output out_6,
  output out_7,
  output out_8,
  output out_9,
  output out_10,
  output out_11,
  output out_12,
  output out_13
);

  wire adder_1_cout, adder_2_cout, adder_3_cout, d_ff_1_qn, d_ff_2_qn, d_ff_3_qn, d_ff_4_qn;

  D_Flip_Flop d_ff_1 (.D(in_1), .clk(C), .Q(out_6), .Qn(d_ff_1_qn));  // open: preset, reset
  D_Flip_Flop d_ff_2 (.D(in_2), .clk(C), .Q(out_8), .Qn(d_ff_2_qn));  // open: preset, reset
  D_Flip_Flop d_ff_3 (.D(in_3), .clk(C), .Q(out_10), .Qn(d_ff_3_qn));  // open: preset, reset
  D_Flip_Flop d_ff_4 (.D(in_4), .clk(C), .Q(out_12), .Qn(d_ff_4_qn));  // open: preset, reset
  Adder #(.width(1)) adder_1 (.a(1'b1), .b(d_ff_1_qn), .out(out_7), .cin(1'b0), .cout(adder_1_cout));
  Adder #(.width(1)) adder_2 (.a(adder_1_cout), .b(d_ff_2_qn), .out(out_9), .cout(adder_2_cout));  // open: cin
  Adder #(.width(1)) adder_3 (.a(adder_2_cout), .b(d_ff_3_qn), .out(out_11), .cout(adder_3_cout));  // open: cin
  Adder #(.width(1)) adder_4 (.a(adder_3_cout), .b(d_ff_4_qn), .out(out_13));  // open: cin, cout
endmodule
