// Logisim project esercizio1.circ as structural Verilog: 1 circuit, main circuit main
module main (
  input  A,
  input  B,
  input  C,
  output out_4
);

  wire and_1_out, and_2_out, not_1_out, not_2_out, xor_1_out;

  xor xor_1 (xor_1_out, B, C);
  not not_1 (not_1_out, A);
  not not_2 (not_2_out, xor_1_out);
  and and_1 (and_1_out, A, xor_1_out);
  and and_2 (and_2_out, not_1_out, not_2_out);
  or or_1 (out_4, and_1_out, and_2_out);
endmodule
