// Logisim project CE_es1_homework3.circ as structural Verilog: 1 circuit, main circuit main
module main (
  input  A,
  input  B,
  input  C,
  output out_4,
  output out_5
);

  wire and_1_out, and_2_out, and_3_out, and_4_out, and_5_out, not_1_out, not_2_out, not_3_out, not_4_out,
       not_5_out, or_1_out, xor_1_out, xor_2_out, xor_3_out;

  xor xor_1 (xor_1_out, B, C);
  xor xor_2 (xor_2_out, B, A);
  not not_1 (not_1_out, B);
  not not_2 (not_2_out, A);
  not not_3 (not_3_out, A);
  and and_1 (and_1_out, not_1_out, not_2_out);
  not not_4 (not_4_out, C);
  not not_5 (not_5_out, xor_1_out);
  xor xor_3 (xor_3_out, B, C);
  and and_2 (and_2_out, xor_2_out, not_4_out);
  or or_1 (or_1_out, not_4_out, C);
  and and_3 (and_3_out, not_3_out, not_5_out);
  and and_4 (and_4_out, and_1_out, or_1_out);
  and and_5 (and_5_out, xor_3_out, A);
  or or_2 (out_5, and_3_out, and_5_out);
  or or_3 (out_4, and_2_out, and_4_out);
endmodule
