// Logisim project CE_es2_homework3.circ as structural Verilog: 1 circuit, main circuit main
module main (
  input  A1,
  input  A2,
  input  A3,
  input  A4,
  input  W,
  input  S,
  output B1,
  output B2,
  output B3,
  output B4
);

  wire and_1_out, and_2_out, and_3_out, and_4_out, and_5_out, and_6_out, and_7_out, and_8_out, and_9_out,
       and_10_out, and_11_out, not_1_out, not_2_out, not_3_out, xor_1_out, xor_2_out, xor_3_out, xor_4_out;

  not not_1 (not_1_out, W);
  not not_2 (not_2_out, S);
  and and_1 (and_1_out, A1, and_5_out);
  and and_2 (and_2_out, A2, and_5_out);
  and and_3 (and_3_out, A3, and_5_out);
  and and_4 (and_4_out, A4, and_5_out);
  and and_5 (and_5_out, W, not_2_out);
  and and_6 (and_6_out, not_1_out, S);
  and and_7 (and_7_out, not_1_out, not_2_out);
  and and_8 (and_8_out, and_6_out, B4);
  not not_3 (not_3_out, and_7_out);
  and and_9 (and_9_out, and_6_out, B1);
  and and_10 (and_10_out, and_6_out, B2);
  and and_11 (and_11_out, and_6_out, B3);
  xor xor_1 (xor_1_out, and_1_out, and_8_out);
  xor xor_2 (xor_2_out, and_2_out, and_9_out);
  xor xor_3 (xor_3_out, and_3_out, and_10_out);
  xor xor_4 (xor_4_out, and_4_out, and_11_out);
  D_Flip_Flop d_ff_1 (.D(xor_1_out), .clk(not_3_out), .Q(B1));  // open: Qn, preset, reset
  D_Flip_Flop d_ff_2 (.D(xor_2_out), .clk(not_3_out), .Q(B2));  // open: Qn, preset, reset
  D_Flip_Flop d_ff_3 (.D(xor_3_out), .clk(not_3_out), .Q(B3));  // open: Qn, preset, reset
  D_Flip_Flop d_ff_4 (.D(xor_4_out), .clk(not_3_out), .Q(B4));  // open: Qn, preset, reset
endmodule
