// Logisim project esercizio_14_esame_07_2019.circ as structural Verilog: 1 circuit, main circuit main
module main (
  input  [3:0] in_1,
  input  in_2,
  output [3:0] out_3
);

  wire not_1_out;
  wire [3:0] adder_1_out, adder_2_out, adder_3_out;

  not not_1 (not_1_out, in_2);
  Adder #(.width(4)) adder_1 (.a(in_1), .b(4'b0000), .out(adder_1_out), .cin(not_1_out));  // open: cout
  Adder #(.width(4)) adder_2 (.a(in_1), .b(4'b1111), .out(adder_2_out), .cin(in_2));  // open: cout
  Adder #(.width(4)) adder_3 (.a(adder_2_out), .b(4'b1111), .out(adder_3_out));  // open: cin, cout
  Multiplexer #(.enable("false"), .width(4)) multiplexer_1 (
    .in0(adder_1_out), .in1(adder_3_out), .out(out_3), .sel(in_2));
endmodule
